// Logisim project ALU.circ as structural Verilog: 1 circuit, main circuit ALU
module ALU (
  input  [31:0] A,
  input  [31:0] B,
  input  [4:0] Shift,
  input  [3:0] Codop,
  input  CarryIn,
  output [31:0] S,
  output [3:0] Flags
);

  wire and_1_out, and_2_out, bitselector_1_out, bitselector_2_out, bitselector_3_out, bitselector_4_out,
       bitselector_5_out, not_1_out, not_2_out, not_3_out, op0101, op0110, op1010, op1011, or_1_out;
  wire [3:0] codop_t;
  wire [4:0] sft, subtractor_5_out, subtractor_6_out;
  wire [31:0] ADC, ASR, BIC, CMN, CMP, EOU, ET, LSL, LSR, MUL, MVN, not_4_out, ORR, RotR, RSB, SBC,
       subtractor_1_out, TST;

  not not_1 (not_1_out, bitselector_1_out);
  BitSelector #(.width(32)) bitselector_1 (.in(S), .out(bitselector_1_out), .sel({5{1'b1}}));
  not not_2 (not_2_out, bitselector_2_out);
  BitSelector #(.width(32)) bitselector_2 (.in(A), .out(bitselector_2_out), .sel({5{1'b1}}));
  not not_3 (not_3_out, bitselector_3_out);
  BitSelector #(.width(32)) bitselector_3 (.in(B), .out(bitselector_3_out), .sel({5{1'b1}}));
  Multiplexer #(.enable("false"), .select(4), .width(32)) multiplexer_1 (
    .in0(ET), .in1(EOU), .in2(LSL), .in3(LSR), .in4(ASR), .in5(ADC), .in6(SBC), .in7(RotR), .in8(TST),
    .in9(RSB), .in10(CMP), .in11(CMN), .in12(ORR), .in13(MUL), .in14(BIC), .in15(MVN), .out(S), .sel(Codop));
  Subtractor #(.width(32)) subtractor_1 (.a(A), .b(B), .out(subtractor_1_out), .bin(CarryIn));  // open: bout
  Comparator #(.width(32)) comparator_1 (.a(S), .b({32{1'b0}}), .eq(Flags[2]), .lt(Flags[3]));  // open: gt
  and and_1 (and_1_out, not_1_out, bitselector_2_out, bitselector_3_out);
  and and_2 (and_2_out, not_2_out, not_3_out, bitselector_1_out);
  Shifter #(.width(32)) shifter_1 (.in(B), .\dist (Shift), .out(LSL));
  Shifter #(.shift("lr"), .width(32)) shifter_2 (.in(B), .\dist (Shift), .out(LSR));
  Shifter #(.shift("ar"), .width(32)) shifter_3 (.in(B), .\dist (Shift), .out(ASR));
  Adder #(.width(32)) adder_1 (.a(A), .b(B), .out(ADC), .cin(CarryIn), .cout(op0101));
  Subtractor #(.width(32)) subtractor_2 (.a(subtractor_1_out), .b(32'h1), .out(SBC), .bout(op0110));  // open: bin
  or or_1 (or_1_out, and_1_out, and_2_out);
  assign ET = A & B;  // AND_Gate and_3, 32 bits wide
  assign EOU = A ^ B;  // XOR_Gate xor_1, 32 bits wide
  Multiplexer #(.enable("false"), .select(4)) multiplexer_2 (
    .in0(1'b0), .in1(1'b0), .in2(1'b0), .in3(1'b0), .in4(1'b0), .in5(or_1_out), .in6(or_1_out), .in7(1'b0),
    .in8(1'b0), .in9(1'b0), .in10(or_1_out), .in11(or_1_out), .in12(1'b0), .in13(1'b0), .in14(1'b0),
    .in15(1'b0), .out(Flags[0]), .sel(codop_t));
  Shifter #(.shift("rr"), .width(32)) shifter_4 (.in(B), .\dist (Shift), .out(RotR));
  Subtractor #(.width(32)) subtractor_3 (.a({32{1'b0}}), .b(A), .out(RSB));  // open: bin, bout
  Subtractor #(.width(32)) subtractor_4 (.a(A), .b(B), .out(CMP), .bout(op1010));  // open: bin
  Adder #(.width(32)) adder_2 (.a(A), .b(B), .out(CMN), .cout(op1011));  // open: cin
  Multiplier #(.width(32)) multiplier_1 (.a(A), .b(B), .out(MUL));  // open: cin, cout
  assign not_4_out = ~B;  // NOT_Gate not_4, 32 bits wide
  Subtractor #(.width(5)) subtractor_5 (.a(sft), .b(5'b00001), .out(subtractor_5_out));  // open: bin, bout
  assign ORR = A | B;  // OR_Gate or_2, 32 bits wide
  assign BIC = A & not_4_out;  // AND_Gate and_4, 32 bits wide
  assign MVN = ~B;  // NOT_Gate not_5, 32 bits wide
  Subtractor #(.width(5)) subtractor_6 (.a({5{1'b0}}), .b(Shift), .out(subtractor_6_out));  // open: bin, bout
  BitSelector #(.width(32)) bitselector_4 (.in(B), .out(bitselector_4_out), .sel(subtractor_6_out));
  BitSelector #(.width(32)) bitselector_5 (.in(B), .out(bitselector_5_out), .sel(subtractor_5_out));
  Multiplexer #(.enable("false"), .select(4)) multiplexer_3 (
    .in0(1'b0), .in1(bitselector_4_out), .in2(bitselector_5_out), .in3(bitselector_5_out), .in4(op0101),
    .in5(op0110), .in6(Flags[3]), .in7(1'b0), .in8(1'b0), .in9(op1010), .in10(op1011), .in11(1'b0),
    .in12(1'b0), .in13(1'b0), .in14(1'b0), .in15(1'b0), .out(Flags[1]), .sel(codop_t));

  // Other names for the same wires on the sheet: Cin = CarryIn; V = Flags[0]; C = Flags[1]; Z = Flags[2];
  //   N = Flags[3]; Result[31:0] = S

  // Notes on the sheet:
  //   Note: for ROR, C = N
  //   Note 2: assume that shift > 0 for LSL and LSR
endmodule
