// Logisim project Ctl_Data_Processing.circ as structural Verilog: 1 circuit, main circuit Data_Processing
module Data_Processing (
  input  Enable,
  input  [15:0] Instruction,
  output [2:0] Rd,
  output [2:0] Rn,
  output [2:0] Rm,
  output [3:0] ALU_Opcode,
  output [3:0] Flags_Update_Mask
);

  wire and_1_out, and_2_out, and_3_out, and_4_out, and_5_out, and_6_out, not_1_out, not_2_out, not_3_out,
       not_4_out, not_5_out, not_6_out, not_7_out, not_8_out, not_9_out, not_10_out, not_11_out, not_12_out,
       not_13_out, not_14_out;
  wire [1:0] and_7_out;

  not not_1 (not_1_out, Instruction[6]);
  not not_2 (not_2_out, Instruction[7]);
  not not_3 (not_3_out, Instruction[9]);
  not not_4 (not_4_out, Instruction[7]);
  not not_5 (not_5_out, Instruction[8]);
  not not_6 (not_6_out, Instruction[7]);
  not not_7 (not_7_out, Instruction[9]);
  not not_8 (not_8_out, Instruction[6]);
  not not_9 (not_9_out, Instruction[7]);
  not not_10 (not_10_out, Instruction[8]);
  not not_11 (not_11_out, Instruction[6]);
  not not_12 (not_12_out, Instruction[8]);
  not not_13 (not_13_out, Instruction[6]);
  not not_14 (not_14_out, Instruction[7]);
  and and_1 (and_1_out, not_1_out, not_2_out, Instruction[8], not_3_out);
  and and_2 (and_2_out, Instruction[6], not_4_out, not_5_out, Instruction[9]);
  and and_3 (and_3_out, Instruction[6], not_6_out, Instruction[8], not_7_out);
  and and_4 (and_4_out, not_8_out, not_9_out, not_10_out, Instruction[9]);
  and and_5 (and_5_out, not_11_out, Instruction[7], not_12_out, Instruction[9]);
  and and_6 (and_6_out, not_13_out, not_14_out, Instruction[8], Instruction[9]);
  not not_15 (and_7_out[1], and_6_out);
  and and_7 (and_7_out[0], and_1_out, and_2_out, and_3_out, and_4_out, and_5_out);
  Multiplexer #(.enable("false"), .width(3)) multiplexer_1 (
    .in0(3'b000), .in1(Instruction[2:0]), .out(Rd), .sel(Enable));
  Multiplexer #(.enable("false"), .width(3)) multiplexer_2 (
    .in0(3'b000), .in1(Instruction[2:0]), .out(Rn), .sel(Enable));
  Multiplexer #(.enable("false"), .width(3)) multiplexer_3 (
    .in0(3'b000), .in1(Instruction[5:3]), .out(Rm), .sel(Enable));
  Multiplexer #(.enable("false"), .width(4)) multiplexer_4 (
    .in0(4'b0000), .in1(Instruction[9:6]), .out(ALU_Opcode), .sel(Enable));
  Multiplexer #(.enable("false"), .width(4)) multiplexer_5 (
    .in0(4'b0000), .in1({2'b11, and_7_out}), .out(Flags_Update_Mask), .sel(Enable));

  // Other names for the same wires on the sheet: Alu_OpCode_t[3:0] = Instruction[9:6]; Rm_t[2:0] = Instruction[5:3];
  //   Rd_t[2:0] = Instruction[2:0]; Rn_t[2:0] = Instruction[2:0]

  // Notes on the sheet:
  //   Note 2: RSB instruction has Rn as 1st operand.
  //   MUL instruction has Rn as 1st operand and Rdm as 2nd operand
  //   For simplification purposes, Rm is used for 1st operand both here and in the ALU.
  //   Note: instructions that does not save the result will still have the second operand as the destination register, the ALU will copy the second register to the destination register
  //   Pull output low on Enable = 0
endmodule
