// Logisim project Ctl_Load_Store.circ as structural Verilog: 1 circuit, main circuit Load_Store
module Load_Store (
  input  [15:0] Instruction,
  input  Enable,
  input  Clk,
  input  Reset,
  input  [31:0] Stack_Pointer,
  output Store,
  output Load,
  output PC_Hold,
  output [2:0] Rmd,
  output [31:0] RAM_Addr
);

  wire ComplementBascule, EntreeBascule, not_1_out;
  wire [31:0] adder_1_out, bit_extender_1_out;

  D_Flip_Flop d_ff_1 (
    .D(EntreeBascule), .clk(Clk), .Q(PC_Hold), .Qn(ComplementBascule), .reset(Reset));  // open: preset
  assign bit_extender_1_out = {{31{Instruction[0]}}, Instruction[0]};  // Bit_Extender bit_extender_1
  not not_1 (not_1_out, Instruction[11]);
  Multiplexer #(.enable("false"), .width(3)) multiplexer_1 (
    .in0(3'b000), .in1(Instruction[10:8]), .out(Rmd), .sel(Enable));
  Multiplexer #(.enable("false")) multiplexer_2 (.in0(1'b0), .in1(Instruction[11]), .out(Load), .sel(Enable));
  Multiplexer #(.enable("false")) multiplexer_3 (.in0(1'b0), .in1(not_1_out), .out(Store), .sel(Enable));
  and and_1 (EntreeBascule, Instruction[11], Enable, ComplementBascule);
  Adder #(.width(32)) adder_1 (.a(Stack_Pointer), .b(bit_extender_1_out), .out(adder_1_out));  // open: cin, cout
  Multiplexer #(.enable("false"), .width(32)) multiplexer_4 (
    .in0({32{1'b0}}), .in1(adder_1_out), .out(RAM_Addr), .sel(Enable));

  // Other names for the same wires on the sheet: Clock = Clk; imm8 = Instruction[0]; OpCode = Instruction[11];
  //   PcHold = PC_Hold; RamAddr[31:0] = RAM_Addr; Rm[2:0] = Instruction[10:8]; StackPoniter[31:0] = Stack_Pointer

  // Notes on the sheet:
  //   Instruction: pull=down
  //   Delay load and hold PC for 1 cycle for the RAM to send out requested data 
endmodule
