// Logisim project Ctl_Opcode_Decoder.circ as structural Verilog: 1 circuit, main circuit Opcode_Decoder
module Opcode_Decoder (
  input  [5:0] Opcode,
  output Shift,
  output Data_Processing,
  output Load_Store,
  output SP_Address,
  output Conditional
);

  wire not_1_out, not_2_out, not_3_out, not_4_out, not_5_out, not_6_out;

  not not_1 (not_1_out, Opcode[0]);
  not not_2 (not_2_out, Opcode[1]);
  not not_3 (not_3_out, Opcode[2]);
  not not_4 (not_4_out, Opcode[3]);
  not not_5 (not_5_out, Opcode[4]);
  not not_6 (not_6_out, Opcode[5]);
  and and_1 (Shift, not_6_out, not_5_out);
  and and_2 (Data_Processing, not_6_out, Opcode[4], not_4_out, not_3_out, not_2_out, not_1_out);
  and and_3 (Load_Store, Opcode[5], not_5_out, not_4_out, Opcode[2]);
  and and_4 (SP_Address, Opcode[5], not_5_out, Opcode[3], Opcode[2]);
  and and_5 (Conditional, Opcode[5], Opcode[4], not_4_out, Opcode[2]);

  // Notes on the sheet:
  //   Load/Store
  //   SP Address
  //   Shift, add, sub, mov
  //   Data Processing
  //   Conditional branch
endmodule
