// Logisim project Ctl_SP_Address.circ as structural Verilog: 1 circuit, main circuit SP_Address
module SP_Address (
  input  [31:0] Stack_Pointer,
  input  [15:0] Instruction,
  input  Enable,
  output [31:0] New_Stack_Pointer,
  output Write_Enable
);

  wire AddOrSub, and_1_out, and_2_out, and_3_out, not_1_out, not_2_out, not_3_out, not_4_out, not_5_out,
       priority_encoder_1_out;
  wire [31:0] adder_1_out, Imm7, multiplexer_1_out, subtractor_1_out;

  not not_1 (not_1_out, Instruction[8]);
  not not_2 (not_2_out, Instruction[9]);
  not not_3 (not_3_out, Instruction[10]);
  not not_4 (not_4_out, Instruction[11]);
  Adder #(.width(32)) adder_1 (.a(Stack_Pointer), .b(Imm7), .out(adder_1_out));  // open: cin, cout
  Subtractor #(.width(32)) subtractor_1 (.a(Stack_Pointer), .b(Imm7), .out(subtractor_1_out));  // open: bin, bout
  assign Imm7 = {{25{1'b0}}, Instruction[6:0]};  // Bit_Extender bit_extender_1
  and and_1 (and_1_out, not_1_out, not_2_out, not_4_out);
  not not_5 (not_5_out, Instruction[7]);
  and and_2 (and_2_out, Instruction[7], and_1_out);
  and and_3 (and_3_out, not_5_out, and_1_out);
  Multiplexer #(.enable("false"), .width(32)) multiplexer_1 (
    .in0(adder_1_out), .in1(subtractor_1_out), .out(multiplexer_1_out), .sel(AddOrSub));
  not not_6 (AddOrSub, priority_encoder_1_out);
  Priority_Encoder #(.select(1)) priority_encoder_1 (
    .in0(and_2_out), .in1(and_3_out), .out(priority_encoder_1_out));  // open: gs, en_out, en_in
  Multiplexer #(.enable("false"), .width(32)) multiplexer_2 (
    .in0(Stack_Pointer), .in1(multiplexer_1_out), .out(New_Stack_Pointer), .sel(Enable));

  assign Write_Enable = Enable;

  // Other names for the same wires on the sheet: New_StackPointer[31:0] = New_Stack_Pointer;
  //   StackPointer[31:0] = Stack_Pointer

  // Notes on the sheet:
  //   Pull output low on Enable = 0
  //   ADD
  //   SUB
endmodule
