// Logisim project Ctl_Shift_Add_Sub_Mov.circ as structural Verilog: 1 circuit, main circuit Shift_Add_Sub_Mov
module Shift_Add_Sub_Mov (
  input  [15:0] Instruction,
  input  Enable,
  output [3:0] Flags_Update_Mask,
  output Carry,
  output Imm32_Enable,
  output [2:0] Rm,
  output [2:0] Rn,
  output [2:0] Rd,
  output [4:0] Imm5,
  output [31:0] Imm32,
  output [3:0] ALU_Opcode
);

  wire ADD, ADD3, and_9_out, ASR, LSL, LSR, MOV, or_1_out, or_4_out, or_8_out, SUB, SUB3;
  wire [2:0] multiplexer_3_out, multiplexer_5_out, or_5_out, priority_encoder_1_out;
  wire [3:0] multiplexer_1_out, multiplexer_10_out;
  wire [4:0] multiplexer_8_out;
  wire [31:0] bit_extender_1_out, bit_extender_2_out, multiplexer_11_out;

  Priority_Encoder priority_encoder_1 (
    .in0(LSL), .in1(LSR), .in2(ASR), .in3(ADD), .in4(SUB), .in5(ADD3), .in6(SUB3), .in7(MOV),
    .out(priority_encoder_1_out));  // open: en_in, gs, en_out
  Multiplexer #(.enable("false"), .select(3), .width(4)) multiplexer_1 (
    .in0(4'b1110), .in1(4'b1110), .in2(4'b1110), .in3(4'b1111), .in4(4'b1111), .in5(4'b1111), .in6(4'b1111),
    .in7(4'b1100), .out(multiplexer_1_out), .sel(priority_encoder_1_out));
  Multiplexer #(.enable("false"), .width(4)) multiplexer_2 (
    .in0(4'b0000), .in1(multiplexer_1_out), .out(Flags_Update_Mask), .sel(Enable));
  and and_1 (LSL, ~Instruction[11], ~Instruction[12], ~Instruction[13]);  // AND_Gate
  and and_2 (LSR, Instruction[11], ~Instruction[12], ~Instruction[13]);  // AND_Gate
  and and_3 (ASR, ~Instruction[11], Instruction[12], ~Instruction[13]);  // AND_Gate
  and and_4 (ADD, ~Instruction[9], ~Instruction[10], Instruction[11], Instruction[12], ~Instruction[13]);  // AND_Gate
  and and_5 (SUB, Instruction[9], ~Instruction[10], Instruction[11], Instruction[12], ~Instruction[13]);  // AND_Gate
  and and_6 (ADD3, ~Instruction[9], Instruction[10], Instruction[11], Instruction[12], ~Instruction[13]);  // AND_Gate
  and and_7 (SUB3, Instruction[9], Instruction[10], Instruction[11], Instruction[12], ~Instruction[13]);  // AND_Gate
  and and_8 (MOV, ~Instruction[11], ~Instruction[12], Instruction[13]);  // AND_Gate
  Multiplexer #(.enable("false"), .width(3)) multiplexer_3 (
    .in0(Instruction[2:0]), .in1(Instruction[10:8]), .out(multiplexer_3_out), .sel(MOV));
  or or_1 (or_1_out, LSL, LSR, ASR);
  Multiplexer #(.enable("false"), .width(3)) multiplexer_4 (
    .in0(3'b000), .in1(multiplexer_3_out), .out(Rd), .sel(Enable));
  or or_2 (Carry, SUB, SUB3, MOV);
  or or_3 (Imm32_Enable, ADD3, SUB3, MOV);
  Multiplexer #(.enable("false"), .width(3)) multiplexer_5 (
    .in0(Instruction[8:6]), .in1(Instruction[5:3]), .out(multiplexer_5_out), .sel(or_1_out));
  Multiplexer #(.enable("false"), .width(3)) multiplexer_6 (
    .in0(3'b000), .in1(multiplexer_5_out), .out(Rm), .sel(Enable));
  Multiplexer #(.enable("false"), .width(3)) multiplexer_7 (
    .in0(3'b000), .in1(Instruction[5:3]), .out(Rn), .sel(Enable));
  and and_9 (and_9_out, Instruction[12], Instruction[11]);
  Multiplexer #(.enable("false"), .width(5)) multiplexer_8 (
    .in0(Instruction[10:6]), .in1({5{1'b0}}), .out(multiplexer_8_out), .sel(or_4_out));
  or or_4 (or_4_out, Instruction[13], and_9_out);
  or or_5 (or_5_out[0], LSR, ADD, ADD3, MOV);
  or or_6 (or_5_out[1], ASR, ADD, SUB3, MOV);
  or or_7 (or_5_out[2], SUB, ADD3, SUB3, MOV);
  Multiplexer #(.enable("false"), .width(5)) multiplexer_9 (
    .in0({5{1'b0}}), .in1(multiplexer_8_out), .out(Imm5), .sel(Enable));
  assign bit_extender_1_out = {{24{1'b0}}, Instruction[7:0]};  // Bit_Extender bit_extender_1
  assign bit_extender_2_out = {{29{1'b0}}, Instruction[8:6]};  // Bit_Extender bit_extender_2
  or or_8 (or_8_out, ADD3, SUB3);
  Multiplexer #(.enable("false"), .select(3), .width(4)) multiplexer_10 (
    .in0(4'b0010), .in1(4'b0011), .in2(4'b0100), .in3(4'b0101), .in4(4'b0110), .in5(4'b1011), .in6(4'b1010),
    .in7(4'b1001), .out(multiplexer_10_out), .sel(or_5_out));
  Multiplexer #(.enable("false"), .width(32)) multiplexer_11 (
    .in0(bit_extender_1_out), .in1(bit_extender_2_out), .out(multiplexer_11_out), .sel(or_8_out));
  Multiplexer #(.enable("false"), .width(32)) multiplexer_12 (
    .in0({32{1'b0}}), .in1(multiplexer_11_out), .out(Imm32), .sel(Imm32_Enable));
  Multiplexer #(.enable("false"), .width(4)) multiplexer_13 (
    .in0(4'b0000), .in1(multiplexer_10_out), .out(ALU_Opcode), .sel(Enable));

  // Other names for the same wires on the sheet: b0 = Instruction[0]; imm8[7:0] = Instruction[7:0];
  //   b1 = Instruction[1]; b2 = Instruction[2]; b3 = Instruction[3]; b4 = Instruction[4]; b5 = Instruction[5];
  //   b6 = Instruction[6]; imm3[2:0] = Instruction[8:6]; b7 = Instruction[7]; b8 = Instruction[8];
  //   b9 = Instruction[9]; b10 = Instruction[10]; codop[3:0] = ALU_Opcode; flag[3:0] = Flags_Update_Mask;
  //   imm32Enable = Imm32_Enable; b11 = Instruction[11]; b12 = Instruction[12]; b13 = Instruction[13];
  //   b14 = Instruction[14]; b15 = Instruction[15]

  // Notes on the sheet:
  //   Note 3: Imm32_Enable forces the use of the immediate for Rm register
  //   Note: ALU uses Rn register for shifts. Use Rn instead of Rm for shifts (immediate) here too
  //   Note 2: MOV uses RSB ALU opcode with Imm8 reversed so that it is copied to output register
  //   Pull output low on Enable = 0
  //   only ADD and SUB use Rm
  //   Enable carry for SUB since it is reversed in ALU
  //   ALU will use Imm32 instead of Rm
endmodule
